# Fritzing sketch Schematics (saved by Fritzing 0.9.3b)
breadboards: 1

parts:
  R1 = Resistor [tolerance=±5% resistance=220 package=THT]
  R2 = Resistor [tolerance=±5% resistance=220 package=THT]
  Raspberry_Pi_1 = Raspberry Pi 3 [part_number=RPI-3-V1.2]  # not connected
  Composant1 = Lithium Ion Cylindrical Battery 3.7v 2200mAh [part_number=1781]
  Composant2 = Lithium Ion Cylindrical Battery 3.7v 2200mAh [part_number=1781]
  Composant3 = Lithium Ion Cylindrical Battery 3.7v 2200mAh [part_number=1781]
  Composant4 = Lithium Ion Cylindrical Battery 3.7v 2200mAh [part_number=1781]
  Composant5 = Lithium Ion Cylindrical Battery 3.7v 2200mAh [part_number=1781]
  Composant6 = Lithium Ion Cylindrical Battery 3.7v 2200mAh [part_number=1781]
  Composant7 = Lithium Ion Cylindrical Battery 3.7v 2200mAh [part_number=1781]
  Composant8 = Lithium Ion Cylindrical Battery 3.7v 2200mAh [part_number=1781]
  Composant9 = Lithium Ion Cylindrical Battery 3.7v 2200mAh [part_number=1781]
  Composant10 = Lithium Ion Cylindrical Battery 3.7v 2200mAh [part_number=1781]

nets:
  N1: R1.Pin_1, R2.Pin_0
  N2: R2.Pin_1, Composant7.negative
  N3: Composant1.negative, Composant2.positive
  N4: Composant2.negative, Composant3.positive
  N5: Composant3.negative, Composant4.positive
  N6: Composant4.negative, Composant5.positive
  N7: Composant5.negative, Composant6.positive
  N8: Composant6.negative, Composant10.positive
  N9: Composant7.positive, Composant8.negative
  N10: Composant8.positive, Composant9.negative
  N11: Composant9.positive, Composant10.negative

custom parts:
  Lithium Ion Cylindrical Battery 3.7v 2200mAh: This lithium ion battery has a capacity of 2200mAh and a protection circuit that provides over-voltage, under-voltage and over-current protection. This cell can provide 2C of peak current (4400mA). Note that these batteries are not designed to sustain such high loads, we suggest keeping any constant current draw under about 0.5C (1 Amp).
